# Fritzing sketch PCB_design (saved by Fritzing 0.9.3b)
circuit board: 9.72673cm x 5.78222cm

parts:
  S1 = Pushbutton [package="[THT]"]
  S2 = Pushbutton [package="[THT]"]
  S3 = Pushbutton [package="[THT]"]
  S4 = Pushbutton [package="[THT]"]
  S5 = Pushbutton [package="[THT]"]
  ATtiny4313 = IC, DIP package, 20 pins [chip_label=ATtiny4313]
  S6 = Pushbutton [package="[THT]"]
  LED3 = smd LED [color="Red (633nm)" package="1206 [SMD]"]
  LED4 = smd LED [color="Red (633nm)" package="1206 [SMD]"]
  LED2 = smd LED [color="Red (633nm)" package="1206 [SMD]"]
  LED5 = smd LED [color="Green (565nm)" package="1206 [SMD]"]
  R1 = Resistor [tolerance=±5% resistance=220 package=THT]
  VCC1 = Battery
  U2 = RJ45 Jack [package=rj45-8]
  U1 = RJ45 Jack [package=rj45-8]
  R2 = Resistor [tolerance=±5% resistance=220 package=THT]
  R3 = Resistor [tolerance=±5% resistance=220 package=THT]
  R4 = Resistor [tolerance=±5% resistance=220 package=THT]

nets (from the pcb view):
  N1: S1.Pin_1, S1.Pin_2, ATtiny4313.pin16
  N2: S1.Pin_3, S2.Pin_3, S3.Pin_1, S3.Pin_2, S4.Pin_3, S4.Pin_4, S5.Pin_3, ATtiny4313.pin20, S6.Pin_3, S6.Pin_4, R1.Pin_0, VCC1.-, R4.Pin_1
  N3: S2.Pin_1, S2.Pin_2, ATtiny4313.pin12
  N4: S3.Pin_3, S3.Pin_4, ATtiny4313.pin17
  N5: S4.Pin_1, S4.Pin_2, ATtiny4313.pin18
  N6: S5.Pin_1, S5.Pin_2, ATtiny4313.pin19
  N7: ATtiny4313.pin1, S6.Pin_1, S6.Pin_2
  N8: ATtiny4313.pin2, U1.1
  N9: ATtiny4313.pin3, LED5.anode
  N10: ATtiny4313.pin4, LED2.anode
  N11: ATtiny4313.pin5, LED3.anode
  N12: ATtiny4313.pin6, LED4.anode
  N13: ATtiny4313.pin7, U2.5
  N14: ATtiny4313.pin8, U2.7
  N15: ATtiny4313.pin9, U2.8
  N16: ATtiny4313.pin10, U2.6
  N17: ATtiny4313.pin11, U2.2
  N18: ATtiny4313.pin13, U2.1
  N19: ATtiny4313.pin14, R2.Pin_1
  N20: ATtiny4313.pin15, R3.Pin_0
  N21: LED3.cathode, LED4.cathode, LED2.cathode, R1.Pin_1
  N22: LED5.cathode, R4.Pin_0
  N23: U2.3, R2.Pin_0
  N24: U1.3, R3.Pin_1
